// Logisim project heitor aluno.circ as structural Verilog: 1 circuit, main circuit main
module main (
  input  in_1,
  input  in_2,
  input  in_3,
  input  in_4,
  input  in_5,
  input  in_6,
  input  in_7,
  input  in_8,
  input  in_9,
  input  in_10,
  input  in_11,
  input  in_12,
  input  in_13,
  input  in_14,
  input  in_15,
  input  in_16,
  input  in_17,
  input  in_18,
  input  in_19,
  input  in_20,
  input  in_21,
  input  in_22,
  input  in_23,
  input  in_24,
  input  in_25,
  input  in_26,
  output out_27,
  output out_28
);

  wire and_1_out, and_2_out, and_3_out, and_4_out, and_5_out, and_6_out, and_7_out, and_8_out, and_10_out,
       not_1_out, not_2_out, not_3_out, not_4_out, not_5_out, not_6_out, not_7_out, not_8_out, not_9_out,
       or_1_out, or_2_out, or_3_out, or_4_out, or_5_out, or_7_out, or_8_out;

  not not_1 (not_1_out, in_10);
  not not_2 (not_2_out, in_11);
  not not_3 (not_3_out, in_15);
  not not_4 (not_4_out, in_16);
  not not_5 (not_5_out, in_18);
  not not_6 (not_6_out, in_19);
  not not_7 (not_7_out, in_20);
  and and_1 (and_1_out, in_1, in_2, in_3);
  not not_8 (not_8_out, in_5);
  and and_2 (and_2_out, in_7, in_8);
  and and_3 (and_3_out, not_1_out, not_2_out);
  or or_1 (or_1_out, in_12, in_13);
  and and_4 (and_4_out, in_14, not_3_out, not_4_out);
  and and_5 (and_5_out, in_17, not_5_out);
  and and_6 (and_6_out, not_6_out, not_7_out);
  and and_7 (and_7_out, in_21, in_22);
  or or_2 (or_2_out, in_23, in_24);
  or or_3 (or_3_out, in_25, in_26);
  and and_8 (and_8_out, in_4, not_8_out);
  or or_4 (or_4_out, and_3_out, or_1_out);
  or or_5 (or_5_out, and_4_out, and_5_out);
  or or_6 (out_27, and_6_out, and_7_out);
  and and_9 (out_28, or_2_out, or_3_out);
  or or_7 (or_7_out, and_1_out, and_8_out);
  or or_8 (or_8_out, in_6, and_2_out);
  not not_9 (not_9_out, in_9);
  and and_10 (and_10_out, not_9_out, or_4_out);
  LED led_1 (.in(or_5_out));
  LED led_2 (.in(or_7_out));
  LED led_3 (.in(or_8_out));
  LED led_4 (.in(and_10_out));
endmodule
